// Logisim project Somadores.circ as structural Verilog: 3 circuits, main circuit main
module main (
  input  in_1,
  input  in_2,
  input  in_3,
  input  in_4,
  input  in_5,
  input  in_6,
  input  in_7,
  input  in_8,
  output out_9,
  output out_10,
  output out_11,
  output out_12,
  output out_13
);

  wire somador_de_1_bit_2_vai_1, somador_de_1_bit_3_vai_1, somador_de_1_bit_4_vai_1;

  Somador_de_1_Bit somador_de_1_bit_1 (.S(out_10), .Vai_1(out_9), .A(in_1), .B(in_2), .C(somador_de_1_bit_2_vai_1));
  Somador_de_1_Bit somador_de_1_bit_2 (
    .S(out_11), .Vai_1(somador_de_1_bit_2_vai_1), .A(in_3), .B(in_4), .C(somador_de_1_bit_3_vai_1));
  Somador_de_1_Bit somador_de_1_bit_3 (
    .S(out_12), .Vai_1(somador_de_1_bit_3_vai_1), .A(in_5), .B(in_6), .C(somador_de_1_bit_4_vai_1));
  Somador_de_1_Bit somador_de_1_bit_4 (.S(out_13), .Vai_1(somador_de_1_bit_4_vai_1), .A(in_7), .B(in_8));  // open: C
endmodule

// Add_1
module Somador_de_1_Bit (
  input  A,
  input  B,
  input  C,
  output S,
  output Vai_1
);

  wire and_1_out, and_2_out, or_1_out, xor_1_out;

  xor xor_1 (xor_1_out, C, B);
  and and_1 (and_1_out, C, B);
  or or_1 (or_1_out, C, B);
  and and_2 (and_2_out, or_1_out, A);
  xor xor_2 (S, xor_1_out, A);
  or or_2 (Vai_1, and_1_out, and_2_out);
endmodule

module Somador_de_4_Bits (
  input  in_1,
  input  in_2,
  input  in_3,
  input  in_4,
  input  in_5,
  input  in_6,
  input  in_7,
  input  in_8,
  output out_9,
  output out_10,
  output out_11,
  output out_12,
  output out_13
);

  wire somador_de_1_bit_2_vai_1, somador_de_1_bit_3_vai_1, somador_de_1_bit_4_vai_1;

  Somador_de_1_Bit somador_de_1_bit_1 (.S(out_10), .Vai_1(out_9), .A(in_1), .B(in_2), .C(somador_de_1_bit_2_vai_1));
  Somador_de_1_Bit somador_de_1_bit_2 (
    .S(out_11), .Vai_1(somador_de_1_bit_2_vai_1), .A(in_3), .B(in_4), .C(somador_de_1_bit_3_vai_1));
  Somador_de_1_Bit somador_de_1_bit_3 (
    .S(out_12), .Vai_1(somador_de_1_bit_3_vai_1), .A(in_5), .B(in_6), .C(somador_de_1_bit_4_vai_1));
  Somador_de_1_Bit somador_de_1_bit_4 (.S(out_13), .Vai_1(somador_de_1_bit_4_vai_1), .A(in_7), .B(in_8));  // open: C
endmodule
